// Logisim project B1_Group5.circ as structural Verilog: 1 circuit, main circuit main
module main (
  input  A3,
  input  A2,
  input  A1,
  input  A0,
  input  B3,
  input  B2,
  input  B1,
  input  B0,
  input  cs2,
  input  cs1,
  input  cs0,
  output C4,
  output F3,
  output F2,
  output F1,
  output F0,
  output C,
  output S,
  output V,
  output Z
);

  wire n7408_1__3__1y, n7408_1__6__2y, n7408_1__8__3y, n7408_1__11__4y, n7408_2__8__3y, n7408_2__11__4y,
       n7432_1__3__1y, n7432_1__6__2y, n7432_1__8__3y, n7483_1__2__s3, n7483_1__6__s2, n7483_1__9__s1,
       n7483_1__14__cout, n7483_1__15__s4, n7486_1__3__1y, n7486_1__6__2y, n7486_1__8__3y, n7486_1__11__4y,
       n7486_2__3__1y, n7486_2__6__2y, n7486_2__8__3y, n74138_1__7__y7, n74138_1__9__y6, n74138_1__10__y5,
       n74138_1__11__y4, n74138_1__12__y3, n74138_1__13__y2, n74138_1__14__y1, n74138_1__15__y0,
       n74157_1__4__y1, n74157_1__7__y2, n74157_1__9__y3, n74157_1__12__y4;

  _7486 u_7486_1 (
    ._1__1A(n74157_1__4__y1), ._2__1B(A0), ._3__1Y(n7486_1__3__1y), ._4__2A(n74157_1__7__y2), ._5__2B(A1),
    ._6__2Y(n7486_1__6__2y), ._7__GND(1'b0), ._14__Vcc(1'b1), ._13__4B(n74157_1__12__y4), ._12__4A(A3),
    ._11__4Y(n7486_1__11__4y), ._10__3B(n74157_1__9__y3), ._9__3A(A2), ._8__3Y(n7486_1__8__3y));
  _7483 u_7483_1 (
    ._1__A4(A3), ._2__S3(n7483_1__2__s3), ._3__A3(A2), ._4__B3(n74157_1__9__y3), ._5__Vcc(1'b1),
    ._6__S2(n7483_1__6__s2), ._7__B2(n74157_1__7__y2), ._8__A2(A1), ._16__B4(n74157_1__12__y4),
    ._15__S4(n7483_1__15__s4), ._14__Cout(n7483_1__14__cout), ._13__Cin(n74138_1__12__y3), ._12__GND(1'b0),
    ._11__B1(n74157_1__4__y1), ._10__A1(A0), ._9__S1(n7483_1__9__s1));
  _74157 u_74157_1 (
    ._1__S(n7408_1__11__4y), ._2__A1(B0), ._3__B1(n74138_1__7__y7), ._4__Y1(n74157_1__4__y1), ._5__A2(B1),
    ._6__B2(n74138_1__7__y7), ._7__Y2(n74157_1__7__y2), ._8__GND(1'b0), ._16__Vcc(1'b1), ._15__G(1'b0),
    ._14__A4(B3), ._13__B4(n74138_1__7__y7), ._12__Y4(n74157_1__12__y4), ._11__A3(B2),
    ._10__B3(n74138_1__7__y7), ._9__Y3(n74157_1__9__y3));
  _74157 u_74157_2 (
    ._1__S(n7408_1__6__2y), ._2__A1(n7486_1__3__1y), ._3__B1(n7483_1__9__s1), ._4__Y1(F0),
    ._5__A2(n7486_1__6__2y), ._6__B2(n7483_1__6__s2), ._7__Y2(F1), ._8__GND(1'b0), ._16__Vcc(1'b1),
    ._15__G(1'b0), ._14__A4(n7486_1__11__4y), ._13__B4(n7483_1__15__s4), ._12__Y4(F3),
    ._11__A3(n7486_1__8__3y), ._10__B3(n7483_1__2__s3), ._9__Y3(F2));
  _7408 u_7408_1 (
    ._1__1A(n74138_1__10__y5), ._2__1B(n74138_1__11__y4), ._3__1Y(n7408_1__3__1y), ._4__2A(n7408_1__3__1y),
    ._5__2B(n74138_1__14__y1), ._6__2Y(n7408_1__6__2y), ._7__GND(1'b0), ._14__Vcc(1'b1),
    ._13__4B(n74138_1__12__y3), ._12__4A(n7408_1__8__3y), ._11__4Y(n7408_1__11__4y),
    ._10__3B(n74138_1__14__y1), ._9__3A(n74138_1__15__y0), ._8__3Y(n7408_1__8__3y));
  _7432 u_7432_1 (
    ._1__1A(F0), ._2__1B(F1), ._3__1Y(n7432_1__3__1y), ._4__2A(n7432_1__3__1y), ._5__2B(F2),
    ._6__2Y(n7432_1__6__2y), ._7__GND(1'b0), ._14__Vcc(1'b1), ._10__3B(n7432_1__6__2y), ._9__3A(F3),
    ._8__3Y(n7432_1__8__3y));  // open: _13__4B, _12__4A, _11__4Y
  _74138 u_74138_1 (
    ._1__A(cs0), ._2__B(cs1), ._3__C(cs2), ._4__G2A(1'b0), ._5__G2B(1'b0), ._6__G1(1'b1),
    ._7__Y7(n74138_1__7__y7), ._8__GND(1'b0), ._16__Vcc(1'b1), ._15__Y0(n74138_1__15__y0),
    ._14__Y1(n74138_1__14__y1), ._13__Y2(n74138_1__13__y2), ._12__Y3(n74138_1__12__y3),
    ._11__Y4(n74138_1__11__y4), ._10__Y5(n74138_1__10__y5), ._9__Y6(n74138_1__9__y6));
  _7408 u_7408_2 (
    ._1__1A(n7483_1__14__cout), ._2__1B(n7408_2__8__3y), ._3__1Y(C), ._4__2A(n7486_2__8__3y),
    ._5__2B(n7408_2__8__3y), ._6__2Y(V), ._7__GND(1'b0), ._14__Vcc(1'b1), ._13__4B(n74138_1__13__y2),
    ._12__4A(n74138_1__14__y1), ._11__4Y(n7408_2__11__4y), ._10__3B(n7408_2__11__4y),
    ._9__3A(n74138_1__9__y6), ._8__3Y(n7408_2__8__3y));
  _7486 u_7486_2 (
    ._1__1A(n7483_1__15__s4), ._2__1B(A3), ._3__1Y(n7486_2__3__1y), ._4__2A(n7486_2__3__1y),
    ._5__2B(n74157_1__12__y4), ._6__2Y(n7486_2__6__2y), ._7__GND(1'b0), ._14__Vcc(1'b1),
    ._13__4B(n7432_1__8__3y), ._12__4A(1'b1), ._11__4Y(Z), ._10__3B(n7483_1__14__cout),
    ._9__3A(n7486_2__6__2y), ._8__3Y(n7486_2__8__3y));

  assign C4 = C;
  assign S = F3;

  // Notes on the sheet:
  //   S2    S1    S0    operation
  //   0        0      0     A+B+1
  //   0        0      1     A XOR B
  //   0        1      0     Transfer A
  //   0        1      1     A+B
  //   1        0      0     Complement A
  //   1        0      1     Complement A
  //   1        1      0     Transfer A
  //   1        1      1     A+1
  //   P3
  //   P0
  //   P2
  //   P1
  //   P4
endmodule
