// Logisim project B1_Group_5_Floating_Point_Adder.circ as structural Verilog: 12 circuits, main circuit main
module main (
  input  [31:0] Input_1,
  input  [31:0] Input_2,
  output Sign,
  output [18:0] Fraction,
  output [11:0] Exponent,
  output [31:0] Output
);

  wire check_if_0_1__0, check_if_0_2__0, check_if_0_3__0, comparator_1_exp_1_exp_2;
  wire [4:0] comparator_1_highest_affordable_diff;
  wire [11:0] comparator_1_larger_exp, normalizer_1_exp, normalizer_2_exp;
  wire [12:0] decimal_viewer_1_out_3, decimal_viewer_2_out_3, decimal_viewer_3_out_3;
  wire [21:0] n22_bit_mux_1_out_4, n22_bit_mux_2_out_4, n22_bit_mux_4_out_4, negator_1_out, negator_2_out;
  wire [31:0] decimal_viewer_1_out_2, decimal_viewer_2_out_2, decimal_viewer_3_out_2, n32_bit_alu_1_f,
       n32_bit_alu_2_f, n32_bit_mux_1_out_4, n32_bit_mux_2_out_4, n32_bit_mux_3_out_4, negator_3_out,
       normalizer_1_mantissa, normalizer_2_mantissa, rounder_1_add_after_round, shifter_1_out;
  wire [31:10] n22_bit_mux_3_out_4;

  Decimal_Viewer decimal_viewer_1 (.in_1(Input_1), .out_3(decimal_viewer_1_out_3), .out_2(decimal_viewer_1_out_2));
  // Probe on decimal_viewer_1_out_2
  Negator #(.width(22)) negator_1 (.in({3'b001, Input_1[18:0]}), .out(negator_1_out));
  // Probe on decimal_viewer_1_out_3
  _22_Bit_Mux u_22_bit_mux_1 (
    .A({3'b001, Input_1[18:0]}), .B(negator_1_out), .S(Input_1[31]), .out_4(n22_bit_mux_1_out_4));
  _22_Bit_Mux u_22_bit_mux_2 (
    .A(n22_bit_mux_4_out_4), .B(n22_bit_mux_1_out_4), .S(comparator_1_exp_1_exp_2),
    .out_4(n22_bit_mux_2_out_4));
  Comparator comparator_1 (
    .Exponent_1(Input_1[30:19]), .Exponent_2(Input_2[30:19]), .Exp_1_Exp_2(comparator_1_exp_1_exp_2),
    .Larger_Exp(comparator_1_larger_exp), .Highest_Affordable_Diff(comparator_1_highest_affordable_diff));
  check_if_0 check_if_0_1 (.\input (Input_1), ._0(check_if_0_1__0));
  Shifter #(.width(32), .shift("ar")) shifter_1 (
    .in({n22_bit_mux_2_out_4, {10{1'b0}}}), .\dist (comparator_1_highest_affordable_diff), .out(shifter_1_out));
  _22_Bit_Mux u_22_bit_mux_3 (
    .A(n22_bit_mux_1_out_4), .B(n22_bit_mux_4_out_4), .S(comparator_1_exp_1_exp_2),
    .out_4(n22_bit_mux_3_out_4));
  _32_Bit_Mux u_32_bit_mux_1 (.A(n32_bit_mux_2_out_4), .B(Input_2), .S(check_if_0_1__0), .out_4(n32_bit_mux_1_out_4));
  Decimal_Viewer decimal_viewer_2 (.in_1(Input_2), .out_3(decimal_viewer_2_out_3), .out_2(decimal_viewer_2_out_2));
  // Probe on decimal_viewer_2_out_2
  Negator #(.width(22)) negator_2 (.in({3'b001, Input_2[18:0]}), .out(negator_2_out));
  _32_Bit_Mux u_32_bit_mux_2 (
    .A({n32_bit_alu_1_f[31], normalizer_2_exp, normalizer_2_mantissa[28:10]}), .B({32{1'b0}}),
    .S(check_if_0_2__0), .out_4(n32_bit_mux_2_out_4));
  // Probe on decimal_viewer_2_out_3
  _22_Bit_Mux u_22_bit_mux_4 (
    .A({3'b001, Input_2[18:0]}), .B(negator_2_out), .S(Input_2[31]), .out_4(n22_bit_mux_4_out_4));
  _32_bit_ALU u_32_bit_alu_1 (
    .A({n22_bit_mux_3_out_4, {10{1'b0}}}), .B(shifter_1_out), .Opcode(3'b000), .F(n32_bit_alu_1_f));  // open: Carry_Flag, Zero_Flag, Sign_Flag
  check_if_0 check_if_0_2 (.\input (n32_bit_alu_1_f), ._0(check_if_0_2__0));
  Negator #(.width(32)) negator_3 (.in(n32_bit_alu_1_f), .out(negator_3_out));
  _32_Bit_Mux u_32_bit_mux_3 (
    .A(n32_bit_alu_1_f), .B(negator_3_out), .S(n32_bit_alu_1_f[31]), .out_4(n32_bit_mux_3_out_4));
  Rounder rounder_1 (.in_1(normalizer_1_mantissa), .Add_after_round(rounder_1_add_after_round));
  check_if_0 check_if_0_3 (.\input (Input_2), ._0(check_if_0_3__0));
  Normalizer normalizer_1 (
    .Significand(n32_bit_mux_3_out_4), .Exponent(comparator_1_larger_exp), .Mantissa(normalizer_1_mantissa),
    .exp(normalizer_1_exp));
  _32_Bit_Mux u_32_bit_mux_4 (
    .A(n32_bit_mux_1_out_4), .B(Input_1), .S(check_if_0_3__0), .out_4({Output[31], Exponent, Fraction}));
  // Probe on decimal_viewer_3_out_2
  Decimal_Viewer decimal_viewer_3 (
    .in_1({Output[31], Exponent, Fraction}), .out_3(decimal_viewer_3_out_3), .out_2(decimal_viewer_3_out_2));
  _32_bit_ALU u_32_bit_alu_2 (
    .A(normalizer_1_mantissa), .B(rounder_1_add_after_round), .Opcode(3'b000), .F(n32_bit_alu_2_f));  // open: Carry_Flag, Zero_Flag, Sign_Flag
  Normalizer normalizer_2 (
    .Significand(n32_bit_alu_2_f), .Exponent(normalizer_1_exp), .Mantissa(normalizer_2_mantissa),
    .exp(normalizer_2_exp));
  // Probe on decimal_viewer_3_out_3

  assign Output[30:0] = {Exponent, Fraction};
  assign Sign = Output[31];

  // Notes on the sheet:
  //   Smaller
  //   Larger
endmodule

// 12 Bit MUX
module _12_Bit_Mux (
  input  [11:0] B,
  input  [11:0] A,
  input  S,
  output [11:0] out_4
);

  _74157 u_74157_1 (
    ._1__S(S), ._2__A1(A[0]), ._3__B1(B[0]), ._4__Y1(out_4[0]), ._5__A2(A[1]), ._6__B2(B[1]),
    ._7__Y2(out_4[1]), ._8__GND(1'b0), ._16__Vcc(1'b1), ._15__G(1'b0), ._14__A4(A[3]), ._13__B4(B[3]),
    ._12__Y4(out_4[3]), ._11__A3(A[2]), ._10__B3(B[2]), ._9__Y3(out_4[2]));
  _74157 u_74157_2 (
    ._1__S(S), ._2__A1(A[4]), ._3__B1(B[4]), ._4__Y1(out_4[4]), ._5__A2(A[5]), ._6__B2(B[5]),
    ._7__Y2(out_4[5]), ._8__GND(1'b0), ._16__Vcc(1'b1), ._15__G(1'b0), ._14__A4(A[7]), ._13__B4(B[7]),
    ._12__Y4(out_4[7]), ._11__A3(A[6]), ._10__B3(B[6]), ._9__Y3(out_4[6]));
  _74157 u_74157_3 (
    ._1__S(S), ._2__A1(A[8]), ._3__B1(B[8]), ._4__Y1(out_4[8]), ._5__A2(A[9]), ._6__B2(B[9]),
    ._7__Y2(out_4[9]), ._8__GND(1'b0), ._16__Vcc(1'b1), ._15__G(1'b0), ._14__A4(A[11]), ._13__B4(B[11]),
    ._12__Y4(out_4[11]), ._11__A3(A[10]), ._10__B3(B[10]), ._9__Y3(out_4[10]));
endmodule

// 32 bit MUX
module _32_Bit_Mux (
  input  [31:0] A,
  input  [31:0] B,
  input  S,
  output [31:0] out_4
);

  wire [11:11] n12_bit_mux_3_out_4;

  _12_Bit_Mux u_12_bit_mux_1 (.B(B[11:0]), .A(A[11:0]), .S(S), .out_4(out_4[11:0]));
  _12_Bit_Mux u_12_bit_mux_2 (.B(B[23:12]), .A(A[23:12]), .S(S), .out_4(out_4[23:12]));
  _12_Bit_Mux u_12_bit_mux_3 (
    .B({4'b0000, B[31:24]}), .A({4'b0000, A[31:24]}), .S(S),
    .out_4({{4{n12_bit_mux_3_out_4[11]}}, out_4[31:24]}));
  // also tied to GND on the sheet: n12_bit_mux_3_out_4[11]
endmodule

module Comparator (
  input  [11:0] Exponent_1,
  input  [11:0] Exponent_2,
  output Exp_1_Exp_2,
  output [11:0] Larger_Exp,
  output [4:0] Highest_Affordable_Diff
);

  wire or_1_out;
  wire [11:0] n12_bit_mux_2_out_4, n16_bit_alu_1_f;
  wire [11:5] n12_bit_mux_3_out_4;
  wire [15:0] n16_bit_alu_2_f;
  wire [15:12] n16_bit_alu_1_f_2;

  _16_bit_ALU u_16_bit_alu_1 (
    .A({4'b0000, Exponent_1}), .B({4'b0000, Exponent_2}), .Opcode(3'b001),
    .F({n16_bit_alu_1_f_2, n16_bit_alu_1_f}), .Sign_Flag(Exp_1_Exp_2));  // open: Carry_Flag, Zero_Flag
  _16_bit_ALU u_16_bit_alu_2 (
    .A({4'b0000, Exponent_2}), .B({4'b0000, Exponent_1}), .Opcode(3'b001), .F(n16_bit_alu_2_f));  // open: Carry_Flag, Zero_Flag, Sign_Flag
  _12_Bit_Mux u_12_bit_mux_1 (.B(Exponent_2), .A(Exponent_1), .S(Exp_1_Exp_2), .out_4(Larger_Exp));
  _12_Bit_Mux u_12_bit_mux_2 (
    .B(n16_bit_alu_2_f[11:0]), .A(n16_bit_alu_1_f), .S(Exp_1_Exp_2), .out_4(n12_bit_mux_2_out_4));
  _12_Bit_Mux u_12_bit_mux_3 (
    .B(12'h1f), .A(n12_bit_mux_2_out_4), .S(or_1_out), .out_4({n12_bit_mux_3_out_4, Highest_Affordable_Diff}));
  or or_1 (or_1_out, n12_bit_mux_2_out_4[5], n12_bit_mux_2_out_4[6], n12_bit_mux_2_out_4[7], n12_bit_mux_2_out_4[8], n12_bit_mux_2_out_4[9], n12_bit_mux_2_out_4[10], n12_bit_mux_2_out_4[11]);

  // Notes on the sheet:
  //   Finds larger exponent
  //   Finds positive difference
endmodule

// 16 Bit ALU
module _16_bit_ALU (
  input  [15:0] A,
  input  [15:0] B,
  input  [2:0] Opcode,
  output Carry_Flag,
  output [15:0] F,
  output Zero_Flag,
  output Sign_Flag
);

  wire [15:0] adder_1_out, and_1_out, multiplexer_1_out, multiplexer_2_out, multiplexer_3_out,
       multiplexer_4_out, not_1_out, or_1_out, shifter_1_out, shifter_2_out, subtractor_1_out, xor_1_out;

  Adder #(.width(16)) adder_1 (.a(A), .b(B), .out(adder_1_out), .cout(Carry_Flag));  // open: cin
  Subtractor #(.width(16)) subtractor_1 (.a(A), .b(B), .out(subtractor_1_out), .bin(Carry_Flag));  // open: bout
  assign and_1_out = A & B;  // AND_Gate and_1, 16 bits wide
  assign or_1_out = A | B;  // OR_Gate or_1, 16 bits wide
  assign not_1_out = ~A;  // NOT_Gate not_1, 16 bits wide
  assign xor_1_out = A ^ B;  // XOR_Gate xor_1, 16 bits wide
  Shifter #(.width(16), .shift("rl")) shifter_1 (.in(A), .\dist (4'b0001), .out(shifter_1_out));
  Shifter #(.width(16), .shift("rr")) shifter_2 (.in(A), .\dist (4'b0001), .out(shifter_2_out));
  Multiplexer #(.width(16), .enable("false")) multiplexer_1 (
    .in0(adder_1_out), .in1(subtractor_1_out), .out(multiplexer_1_out), .sel(Opcode[0]));
  Multiplexer #(.width(16), .enable("false")) multiplexer_2 (
    .in0(and_1_out), .in1(or_1_out), .out(multiplexer_2_out), .sel(Opcode[0]));
  Multiplexer #(.width(16), .enable("false")) multiplexer_3 (
    .in0(not_1_out), .in1(xor_1_out), .out(multiplexer_3_out), .sel(Opcode[0]));
  Multiplexer #(.width(16), .enable("false")) multiplexer_4 (
    .in0(shifter_1_out), .in1(shifter_2_out), .out(multiplexer_4_out), .sel(Opcode[0]));
  nor nor_1 (Zero_Flag, F[0], F[1], F[2], F[3], F[4], F[5], F[6], F[7], F[8], F[9], F[10], F[11], F[12], F[13], F[14], F[15]);
  Multiplexer #(.select(2), .width(16), .enable("false")) multiplexer_5 (
    .in0(multiplexer_1_out), .in1(multiplexer_2_out), .in2(multiplexer_3_out), .in3(multiplexer_4_out),
    .out(F), .sel(Opcode[2:1]));

  assign Sign_Flag = F[15];

  // Notes on the sheet:
  //   000 for addition, 001 for subtraction
  //   100 for not
endmodule

module _32_bit_ALU (
  input  [31:0] A,
  input  [31:0] B,
  input  [2:0] Opcode,
  output Carry_Flag,
  output [31:0] F,
  output Zero_Flag,
  output Sign_Flag
);

  wire [31:0] adder_1_out, and_1_out, multiplexer_1_out, multiplexer_2_out, multiplexer_3_out,
       multiplexer_4_out, not_1_out, or_1_out, shifter_1_out, shifter_2_out, subtractor_1_out, xor_1_out;

  Adder #(.width(32)) adder_1 (.a(A), .b(B), .out(adder_1_out), .cout(Carry_Flag));  // open: cin
  Subtractor #(.width(32)) subtractor_1 (.a(A), .b(B), .out(subtractor_1_out), .bin(Carry_Flag));  // open: bout
  assign and_1_out = A & B;  // AND_Gate and_1, 32 bits wide
  assign or_1_out = A | B;  // OR_Gate or_1, 32 bits wide
  assign not_1_out = ~A;  // NOT_Gate not_1, 32 bits wide
  assign xor_1_out = A ^ B;  // XOR_Gate xor_1, 32 bits wide
  Shifter #(.width(32), .shift("rl")) shifter_1 (.in(A), .\dist (5'b00001), .out(shifter_1_out));
  Shifter #(.width(32), .shift("rr")) shifter_2 (.in(A), .\dist (5'b00001), .out(shifter_2_out));
  Multiplexer #(.width(32), .enable("false")) multiplexer_1 (
    .in0(adder_1_out), .in1(subtractor_1_out), .out(multiplexer_1_out), .sel(Opcode[0]));
  Multiplexer #(.width(32), .enable("false")) multiplexer_2 (
    .in0(and_1_out), .in1(or_1_out), .out(multiplexer_2_out), .sel(Opcode[0]));
  Multiplexer #(.width(32), .enable("false")) multiplexer_3 (
    .in0(not_1_out), .in1(xor_1_out), .out(multiplexer_3_out), .sel(Opcode[0]));
  Multiplexer #(.width(32), .enable("false")) multiplexer_4 (
    .in0(shifter_1_out), .in1(shifter_2_out), .out(multiplexer_4_out), .sel(Opcode[0]));
  Multiplexer #(.select(2), .width(32), .enable("false")) multiplexer_5 (
    .in0(multiplexer_1_out), .in1(multiplexer_2_out), .in2(multiplexer_3_out), .in3(multiplexer_4_out),
    .out(F), .sel(Opcode[2:1]));
  nor nor_1 (Zero_Flag, F[0], F[1], F[2], F[3], F[4], F[5], F[6], F[7], F[8], F[9], F[10], F[11], F[12], F[13], F[14], F[15], F[16], F[17], F[18], F[19], F[20], F[21], F[22], F[23], F[24], F[25], F[26], F[27], F[28], F[29], F[30], F[31]);

  assign Sign_Flag = F[31];

  // Notes on the sheet:
  //   000 for addition, 001 for subtraction
  //   100 for not
endmodule

// 0 check
module check_if_0 (
  input  [31:0] \input ,
  output _0
);

  wire n32_bit_alu_1_sign_flag;

  _32_bit_ALU u_32_bit_alu_1 (
    .A({32{1'b0}}), .B({1'b0, \input [30:0]}), .Opcode(3'b001), .Sign_Flag(n32_bit_alu_1_sign_flag));  // open: Carry_Flag, F, Zero_Flag
  not not_1 (_0, n32_bit_alu_1_sign_flag);
endmodule

// 22 bit MUX
module _22_Bit_Mux (
  input  [21:0] A,
  input  [21:0] B,
  input  S,
  output [21:0] out_4
);

  wire [31:31] n32_bit_mux_1_out_4;

  _32_Bit_Mux u_32_bit_mux_1 (
    .A({{10{1'b0}}, A}), .B({{10{1'b0}}, B}), .S(S), .out_4({{10{n32_bit_mux_1_out_4[31]}}, out_4}));
  // also tied to GND on the sheet: n32_bit_mux_1_out_4[31]
endmodule

module Normalizer (
  input  [31:0] Significand,
  input  [11:0] Exponent,
  output [31:0] Mantissa,
  output [11:0] exp
);

  wire n16_bit_alu_1_sign_flag;
  wire [4:0] bitfinder_1_index;
  wire [15:0] n16_bit_alu_1_f, negator_1_out;
  wire [15:12] n16_bit_alu_2_f;
  wire [31:0] shifter_1_out, shifter_2_out;

  BitFinder #(.width(32), .\type ("high1")) bitfinder_1 (.in(Significand), .index(bitfinder_1_index));  // open: found
  _16_bit_ALU u_16_bit_alu_1 (
    .A(16'h1d), .B({{11{1'b0}}, bitfinder_1_index}), .Opcode(3'b001), .F(n16_bit_alu_1_f),
    .Sign_Flag(n16_bit_alu_1_sign_flag));  // open: Carry_Flag, Zero_Flag
  Shifter #(.width(32)) shifter_1 (.in(Significand), .\dist (n16_bit_alu_1_f[4:0]), .out(shifter_1_out));
  Shifter #(.width(32), .shift("lr")) shifter_2 (.in(Significand), .\dist (5'b00001), .out(shifter_2_out));
  Negator #(.width(16)) negator_1 (.in(n16_bit_alu_1_f), .out(negator_1_out));
  _16_bit_ALU u_16_bit_alu_2 (
    .A({4'b0000, Exponent}), .B(negator_1_out), .Opcode(3'b000), .F({n16_bit_alu_2_f, exp}));  // open: Carry_Flag, Zero_Flag, Sign_Flag
  _32_Bit_Mux u_32_bit_mux_1 (.A(shifter_1_out), .B(shifter_2_out), .S(n16_bit_alu_1_sign_flag), .out_4(Mantissa));
endmodule

module Rounder (
  input  [31:0] in_1,
  output [31:0] Add_after_round
);

  wire n7432_1__3__1y, n7432_1__6__2y, n7432_1__8__3y, n7432_1__11__4y, n7432_2__3__1y, n7432_2__6__2y,
       n7432_2__8__3y, n7432_2__11__4y, n7432_3__3__1y;

  _7432 u_7432_1 (
    ._1__1A(in_1[0]), ._2__1B(in_1[1]), ._3__1Y(n7432_1__3__1y), ._4__2A(n7432_1__3__1y), ._5__2B(in_1[2]),
    ._6__2Y(n7432_1__6__2y), ._7__GND(in_1[31]), ._14__Vcc(1'b1), ._13__4B(in_1[4]),
    ._12__4A(n7432_1__8__3y), ._11__4Y(n7432_1__11__4y), ._10__3B(in_1[3]), ._9__3A(n7432_1__6__2y),
    ._8__3Y(n7432_1__8__3y));
  _7432 u_7432_2 (
    ._1__1A(in_1[5]), ._2__1B(n7432_1__11__4y), ._3__1Y(n7432_2__3__1y), ._4__2A(n7432_2__3__1y),
    ._5__2B(in_1[6]), ._6__2Y(n7432_2__6__2y), ._7__GND(in_1[31]), ._14__Vcc(1'b1), ._13__4B(in_1[8]),
    ._12__4A(n7432_2__8__3y), ._11__4Y(n7432_2__11__4y), ._10__3B(in_1[7]), ._9__3A(n7432_2__6__2y),
    ._8__3Y(n7432_2__8__3y));
  _7432 u_7432_3 (
    ._1__1A(in_1[10]), ._2__1B(n7432_2__11__4y), ._3__1Y(n7432_3__3__1y), ._7__GND(in_1[31]), ._14__Vcc(1'b1));  // open: _4__2A, _5__2B, _6__2Y, _13__4B, _12__4A, _11__4Y, _10__3B, _9__3A, _8__3Y
  _7408 u_7408_1 (
    ._1__1A(n7432_3__3__1y), ._2__1B(in_1[9]), ._3__1Y(Add_after_round[9]), ._7__GND(in_1[31]),
    ._14__Vcc(1'b1));  // open: _4__2A, _5__2B, _6__2Y, _13__4B, _12__4A, _11__4Y, _10__3B, _9__3A, _8__3Y

  assign {Add_after_round[31:10], Add_after_round[8:0]} = {31{1'b0}};
  assign in_1[30:11] = {20{in_1[31]}};
  // also tied to GND on the sheet: in_1[31]
endmodule

module Block_Diagram (
  input  [31:0] Input_1,
  input  [31:0] Input_2,
  input  [31:0] Output,
  output Sign_Bit,
  output [11:0] Exponent,
  output [18:0] Fraction
);

  main main_1 (
    .Input_1(Input_1), .Input_2(Input_2), .Sign(Sign_Bit), .Fraction(Fraction), .Exponent(Exponent),
    .Output(Output));
endmodule

module Decimal_Viewer (
  input  [31:0] in_1,
  output [31:0] out_2,
  output [12:0] out_3
);

  wire check_if_0_1__0;
  wire [31:0] divider_1_out, multiplexer_2_out, multiplier_1_cout, multiplier_1_out, negator_1_out;

  check_if_0 check_if_0_1 (.\input (in_1), ._0(check_if_0_1__0));
  Subtractor #(.width(13)) subtractor_1 (.a({1'b0, in_1[30:19]}), .b(13'h7ff), .out(out_3));  // open: bin, bout
  Multiplier #(.width(32)) multiplier_1 (
    .a({13'h1, in_1[18:0]}), .b(32'h186a0), .out(multiplier_1_out), .cout(multiplier_1_cout));  // open: cin
  Divider #(.width(32)) divider_1 (
    .a(multiplier_1_out), .b(32'h80000), .out(divider_1_out), .upper(multiplier_1_cout));  // open: rem
  Multiplexer #(.width(32), .enable("false")) multiplexer_1 (
    .in0(multiplexer_2_out), .in1({32{1'b0}}), .out(out_2), .sel(check_if_0_1__0));
  Multiplexer #(.width(32), .enable("false")) multiplexer_2 (
    .in0(divider_1_out), .in1(negator_1_out), .out(multiplexer_2_out), .sel(in_1[31]));
  Negator #(.width(32)) negator_1 (.in(divider_1_out), .out(negator_1_out));
  // Probe on out_3
  // Probe on out_2
endmodule
